# Fritzing sketch Door (saved by Fritzing 0.8.3b)
circuit board: 7.38479cm x 5.72911cm
breadboards: 1

parts:
  Part1 = Arduino Uno (Rev3)
  R1 = Resistor [tolerance=±5% resistance=220 package=THT]
  R2 = Resistor [tolerance=±5% resistance=2.2k package=THT]
  J2 = screw terminal, 3 pins
  J1 = screw terminal, 4 pins
  Part2 = Real Time Clock Module - DS1307 RTC Breakout Board
  R3 = Resistor [tolerance=±5% resistance=2.2k package=THT]
  R4 = Resistor [tolerance=±5% resistance=2.2k package=THT]
  R5 = Resistor [tolerance=±5% resistance=330 package=THT]
  Q1 = NPN-Transistor [package="TO92 [THT]"]
  R8 = Resistor [tolerance=±5% resistance=680 package=THT]
  LED1 = LED - 5mm [color="Yellow (585nm)" package="5 mm [THT]"]
  R9 = Resistor [tolerance=±5% resistance=2.2k package=THT]
  LED2 = LED - 5mm [color="Green (565nm)" package="5 mm [THT]"]

nets:
  N1: Part1.A0, R2.Pin_1, J1.pin1
  N2: Part1.A4/SDA, Part2.SDA, R3.Pin_1
  N3: Part1.A5/SCL, Part2.SCL, R4.Pin_1
  GND: Part1.GND, J2.pin3, J1.pin2, J1.pin4, Part2.GND, Q1.E
  5V: Part1.5V, R2.Pin_0, J2.pin1, Part2.5V, R3.Pin_0, R4.Pin_0, R8.Pin_0, R9.Pin_0, LED2.anode
  N4: Part1.D2, R1.Pin_0
  N5: Part1.D3_PWM, R5.Pin_0
  N6: Part1.D4, J2.pin2
  N7: R1.Pin_1, J1.pin3
  N8: Part2.SQW, Q1.B, R9.Pin_1
  N9: R5.Pin_1, LED2.cathode
  N10: Q1.C, LED1.cathode
  N11: R8.Pin_1, LED1.anode

notes:
  1w Reader:
  1. 1w+ / Green
  2. 1w- / Blue
  3. LED+ / Orange
  4. LED- / Yellow
  Relay board:
  1. Vcc
  2. CH1
  3. GND
